# Fritzing sketch connecties (saved by Fritzing 0.9.3b)

parts:
  Part1 = Arduino Uno (Rev3)
  Part2 = Soil Moisture Sensor
  J1 = Basic Servo

nets:
  N1: Part1.A0, Part2.SIG
  N2: Part1.D11_PWM/MOSI, J1.pulse
  3V3: Part1.3V3, Part2.VCC
  5V: Part1.5V, J1.vcc
  GND: Part1.GND, Part2.GND, J1.gnd
